// Logisim project hack of logisim.circ as structural Verilog: 10 circuits, main circuit main
module main (
  input  in_1,
  input  [15:0] in_2,
  output [15:0] out_3
);

  wire clock_1_out;

  Clock clock_1 (.out(clock_1_out));
  D_Flip_Flop d_ff_1 (.clk(clock_1_out), .D(in_2[0]), .Q(out_3[0]), .en(in_1));  // open: Qn, preset, reset
  D_Flip_Flop d_ff_2 (.clk(clock_1_out), .D(in_2[1]), .Q(out_3[1]), .en(in_1));  // open: Qn, preset, reset
  D_Flip_Flop d_ff_3 (.clk(clock_1_out), .D(in_2[2]), .Q(out_3[2]), .en(in_1));  // open: Qn, preset, reset
  D_Flip_Flop d_ff_4 (.clk(clock_1_out), .D(in_2[3]), .Q(out_3[3]), .en(in_1));  // open: Qn, preset, reset
  D_Flip_Flop d_ff_5 (.clk(clock_1_out), .D(in_2[4]), .Q(out_3[4]), .en(in_1));  // open: Qn, preset, reset
  D_Flip_Flop d_ff_6 (.clk(clock_1_out), .D(in_2[5]), .Q(out_3[5]), .en(in_1));  // open: Qn, preset, reset
  D_Flip_Flop d_ff_7 (.clk(clock_1_out), .D(in_2[6]), .Q(out_3[6]), .en(in_1));  // open: Qn, preset, reset
  D_Flip_Flop d_ff_8 (.clk(clock_1_out), .D(in_2[7]), .Q(out_3[7]), .en(in_1));  // open: Qn, preset, reset
  D_Flip_Flop d_ff_9 (.clk(clock_1_out), .D(in_2[8]), .Q(out_3[8]), .en(in_1));  // open: Qn, preset, reset
  D_Flip_Flop d_ff_10 (.clk(clock_1_out), .D(in_2[9]), .Q(out_3[9]), .en(in_1));  // open: Qn, preset, reset
  D_Flip_Flop d_ff_11 (.clk(clock_1_out), .D(in_2[10]), .Q(out_3[10]), .en(in_1));  // open: Qn, preset, reset
  D_Flip_Flop d_ff_12 (.clk(clock_1_out), .D(in_2[11]), .Q(out_3[11]), .en(in_1));  // open: Qn, preset, reset
  D_Flip_Flop d_ff_13 (.clk(clock_1_out), .D(in_2[12]), .Q(out_3[12]), .en(in_1));  // open: Qn, preset, reset
  D_Flip_Flop d_ff_14 (.clk(clock_1_out), .D(in_2[13]), .Q(out_3[13]), .en(in_1));  // open: Qn, preset, reset
  D_Flip_Flop d_ff_15 (.clk(clock_1_out), .D(in_2[14]), .Q(out_3[14]), .en(in_1));  // open: Qn, preset, reset
  D_Flip_Flop d_ff_16 (.clk(clock_1_out), .D(in_2[15]), .Q(out_3[15]), .en(in_1));  // open: Qn, preset, reset
endmodule

module Register (
  input  in_1,
  input  [15:0] in_2,
  output [15:0] out_3
);

  wire clock_1_out;

  Clock clock_1 (.out(clock_1_out));
  D_Flip_Flop d_ff_1 (.clk(clock_1_out), .D(in_2[0]), .Q(out_3[0]), .en(in_1));  // open: Qn, preset, reset
  D_Flip_Flop d_ff_2 (.clk(clock_1_out), .D(in_2[1]), .Q(out_3[1]), .en(in_1));  // open: Qn, preset, reset
  D_Flip_Flop d_ff_3 (.clk(clock_1_out), .D(in_2[2]), .Q(out_3[2]), .en(in_1));  // open: Qn, preset, reset
  D_Flip_Flop d_ff_4 (.clk(clock_1_out), .D(in_2[3]), .Q(out_3[3]), .en(in_1));  // open: Qn, preset, reset
  D_Flip_Flop d_ff_5 (.clk(clock_1_out), .D(in_2[4]), .Q(out_3[4]), .en(in_1));  // open: Qn, preset, reset
  D_Flip_Flop d_ff_6 (.clk(clock_1_out), .D(in_2[5]), .Q(out_3[5]), .en(in_1));  // open: Qn, preset, reset
  D_Flip_Flop d_ff_7 (.clk(clock_1_out), .D(in_2[6]), .Q(out_3[6]), .en(in_1));  // open: Qn, preset, reset
  D_Flip_Flop d_ff_8 (.clk(clock_1_out), .D(in_2[7]), .Q(out_3[7]), .en(in_1));  // open: Qn, preset, reset
  D_Flip_Flop d_ff_9 (.clk(clock_1_out), .D(in_2[8]), .Q(out_3[8]), .en(in_1));  // open: Qn, preset, reset
  D_Flip_Flop d_ff_10 (.clk(clock_1_out), .D(in_2[9]), .Q(out_3[9]), .en(in_1));  // open: Qn, preset, reset
  D_Flip_Flop d_ff_11 (.clk(clock_1_out), .D(in_2[10]), .Q(out_3[10]), .en(in_1));  // open: Qn, preset, reset
  D_Flip_Flop d_ff_12 (.clk(clock_1_out), .D(in_2[11]), .Q(out_3[11]), .en(in_1));  // open: Qn, preset, reset
  D_Flip_Flop d_ff_13 (.clk(clock_1_out), .D(in_2[12]), .Q(out_3[12]), .en(in_1));  // open: Qn, preset, reset
  D_Flip_Flop d_ff_14 (.clk(clock_1_out), .D(in_2[13]), .Q(out_3[13]), .en(in_1));  // open: Qn, preset, reset
  D_Flip_Flop d_ff_15 (.clk(clock_1_out), .D(in_2[14]), .Q(out_3[14]), .en(in_1));  // open: Qn, preset, reset
  D_Flip_Flop d_ff_16 (.clk(clock_1_out), .D(in_2[15]), .Q(out_3[15]), .en(in_1));  // open: Qn, preset, reset
endmodule

module FullAdder (
  input  in_1,
  input  in_2,
  input  in_3,
  output out_4,
  output out_5
);

  wire and_1_out, and_2_out, xor_1_out;

  xor xor_1 (xor_1_out, in_1, in_2);
  and and_1 (and_1_out, xor_1_out, in_3);
  and and_2 (and_2_out, in_2, in_1);
  xor xor_2 (out_4, xor_1_out, in_3);
  or or_1 (out_5, and_1_out, and_2_out);
endmodule

module _16adder (
  input  [15:0] in_1,
  input  [15:0] in_2,
  output [15:0] out_3
);

  wire fulladder_1_out_5, fulladder_2_out_5, fulladder_3_out_5, fulladder_4_out_5, fulladder_5_out_5,
       fulladder_6_out_5, fulladder_7_out_5, fulladder_8_out_5, fulladder_9_out_5, fulladder_10_out_5,
       fulladder_11_out_5, fulladder_12_out_5, fulladder_13_out_5, fulladder_14_out_5, fulladder_15_out_5;

  FullAdder fulladder_1 (.in_1(in_1[0]), .in_2(in_2[0]), .in_3(1'b0), .out_4(out_3[0]), .out_5(fulladder_1_out_5));
  FullAdder fulladder_2 (
    .in_1(in_1[1]), .in_2(in_2[1]), .in_3(fulladder_1_out_5), .out_4(out_3[1]), .out_5(fulladder_2_out_5));
  FullAdder fulladder_3 (
    .in_1(in_1[2]), .in_2(in_2[2]), .in_3(fulladder_2_out_5), .out_4(out_3[2]), .out_5(fulladder_3_out_5));
  FullAdder fulladder_4 (
    .in_1(in_1[3]), .in_2(in_2[3]), .in_3(fulladder_3_out_5), .out_4(out_3[3]), .out_5(fulladder_4_out_5));
  FullAdder fulladder_5 (
    .in_1(in_1[4]), .in_2(in_2[4]), .in_3(fulladder_4_out_5), .out_4(out_3[4]), .out_5(fulladder_5_out_5));
  FullAdder fulladder_6 (
    .in_1(in_1[5]), .in_2(in_2[5]), .in_3(fulladder_5_out_5), .out_4(out_3[5]), .out_5(fulladder_6_out_5));
  FullAdder fulladder_7 (
    .in_1(in_1[6]), .in_2(in_2[6]), .in_3(fulladder_6_out_5), .out_4(out_3[6]), .out_5(fulladder_7_out_5));
  FullAdder fulladder_8 (
    .in_1(in_1[7]), .in_2(in_2[7]), .in_3(fulladder_7_out_5), .out_4(out_3[7]), .out_5(fulladder_8_out_5));
  FullAdder fulladder_9 (
    .in_1(in_1[8]), .in_2(in_2[8]), .in_3(fulladder_8_out_5), .out_4(out_3[8]), .out_5(fulladder_9_out_5));
  FullAdder fulladder_10 (
    .in_1(in_1[9]), .in_2(in_2[9]), .in_3(fulladder_9_out_5), .out_4(out_3[9]), .out_5(fulladder_10_out_5));
  FullAdder fulladder_11 (
    .in_1(in_1[10]), .in_2(in_2[10]), .in_3(fulladder_10_out_5), .out_4(out_3[10]), .out_5(fulladder_11_out_5));
  FullAdder fulladder_12 (
    .in_1(in_1[11]), .in_2(in_2[11]), .in_3(fulladder_11_out_5), .out_4(out_3[11]), .out_5(fulladder_12_out_5));
  FullAdder fulladder_13 (
    .in_1(in_1[12]), .in_2(in_2[12]), .in_3(fulladder_12_out_5), .out_4(out_3[12]), .out_5(fulladder_13_out_5));
  FullAdder fulladder_14 (
    .in_1(in_1[13]), .in_2(in_2[13]), .in_3(fulladder_13_out_5), .out_4(out_3[13]), .out_5(fulladder_14_out_5));
  FullAdder fulladder_15 (
    .in_1(in_1[14]), .in_2(in_2[14]), .in_3(fulladder_14_out_5), .out_4(out_3[14]), .out_5(fulladder_15_out_5));
  FullAdder fulladder_16 (
    .in_1(in_1[15]), .in_2(in_2[15]), .in_3(fulladder_15_out_5), .out_4(out_3[15]));  // open: out_5
endmodule

module ALU (
  input  [15:0] in_1,
  input  in_2,
  input  in_3,
  input  [15:0] in_4,
  input  in_5,
  input  in_6,
  input  in_7,
  input  in_8,
  output out_9,
  output [15:0] out_10,
  output out_11
);

  wire [1:0] and_3_out, and_3_out_2, and_4_out;
  wire [7:0] and_2_out, not_4_out, not_4_out_2;
  wire [15:0] and_1_out, multiplexer_1_out, multiplexer_2_out, multiplexer_3_out, multiplexer_4_out,
       multiplexer_5_out, n16adder_1_out_3, not_1_out, not_2_out, not_3_out;

  Multiplexer #(.width(16), .enable("false")) multiplexer_1 (
    .in0(in_1), .in1({16{1'b0}}), .out(multiplexer_1_out), .sel(in_2));
  assign not_1_out = ~multiplexer_1_out;  // NOT_Gate not_1, 16 bits wide
  Multiplexer #(.width(16), .enable("false")) multiplexer_2 (
    .in0(in_4), .in1({16{1'b0}}), .out(multiplexer_2_out), .sel(in_5));
  assign not_2_out = ~multiplexer_2_out;  // NOT_Gate not_2, 16 bits wide
  Multiplexer #(.width(16), .enable("false")) multiplexer_3 (
    .in0(multiplexer_1_out), .in1(not_1_out), .out(multiplexer_3_out), .sel(in_3));
  Multiplexer #(.width(16), .enable("false")) multiplexer_4 (
    .in0(multiplexer_2_out), .in1(not_2_out), .out(multiplexer_4_out), .sel(in_6));
  assign and_1_out = multiplexer_3_out & multiplexer_4_out;  // AND_Gate and_1, 16 bits wide
  _16adder u_16adder_1 (.in_1(multiplexer_3_out), .in_2(multiplexer_4_out), .out_3(n16adder_1_out_3));
  Multiplexer #(.width(16), .enable("false")) multiplexer_5 (
    .in0(and_1_out), .in1(n16adder_1_out_3), .out(multiplexer_5_out), .sel(in_7));
  assign not_3_out = ~multiplexer_5_out;  // NOT_Gate not_3, 16 bits wide
  Multiplexer #(.width(16), .enable("false")) multiplexer_6 (
    .in0(multiplexer_5_out), .in1(not_3_out), .out({out_9, out_10[14:0]}), .sel(in_8));
  assign {not_4_out_2, not_4_out} = ~{out_9, out_10[14:0]};  // NOT_Gate not_4, 16 bits wide
  assign and_2_out = not_4_out & not_4_out_2;  // AND_Gate and_2, 8 bits wide
  assign {and_3_out_2, and_3_out} = and_2_out[3:0] & and_2_out[7:4];  // AND_Gate and_3, 4 bits wide
  assign and_4_out = and_3_out & and_3_out_2;  // AND_Gate and_4, 2 bits wide
  and and_5 (out_11, and_4_out[0], and_4_out[1]);

  assign out_10[15] = out_9;
endmodule

module _4RAM (
  input  in_1,
  input  [15:0] in_2,
  input  [1:0] in_3,
  output [15:0] out_4
);

  wire [15:0] demultiplexer_1_out0, demultiplexer_1_out1, demultiplexer_1_out2, demultiplexer_1_out3,
       register_1_out_3, register_2_out_3, register_3_out_3, register_4_out_3;

  Demultiplexer #(.select(2), .width(16), .enable("false")) demultiplexer_1 (
    .out0(demultiplexer_1_out0), .out1(demultiplexer_1_out1), .out2(demultiplexer_1_out2),
    .out3(demultiplexer_1_out3), .in(in_2), .sel(in_3));
  Register register_1 (.in_1(in_1), .in_2(demultiplexer_1_out0), .out_3(register_1_out_3));
  Register register_2 (.in_1(in_1), .in_2(demultiplexer_1_out1), .out_3(register_2_out_3));
  Register register_3 (.in_1(in_1), .in_2(demultiplexer_1_out2), .out_3(register_3_out_3));
  Register register_4 (.in_1(in_1), .in_2(demultiplexer_1_out3), .out_3(register_4_out_3));
  Multiplexer #(.select(2), .width(16), .enable("false")) multiplexer_1 (
    .in0(register_1_out_3), .in1(register_2_out_3), .in2(register_3_out_3), .in3(register_4_out_3),
    .out(out_4), .sel(in_3));
endmodule

module _16RAM (
  input  in_1,
  input  [15:0] in_2,
  input  [3:0] in_3,
  output [15:0] out_4
);

  wire [15:0] demultiplexer_1_out0, demultiplexer_1_out1, demultiplexer_1_out2, demultiplexer_1_out3,
       n4ram_1_out_4, n4ram_2_out_4, n4ram_3_out_4, n4ram_4_out_4;

  Demultiplexer #(.select(2), .width(16), .enable("false")) demultiplexer_1 (
    .out0(demultiplexer_1_out0), .out1(demultiplexer_1_out1), .out2(demultiplexer_1_out2),
    .out3(demultiplexer_1_out3), .in(in_2), .sel(in_3[3:2]));
  ROM #(.dataWidth(16)) rom_1 ();  // open: addr, data, sel
  RAM ram_1 ();  // open: addr, data, sel, clk, ld, clr
  _4RAM u_4ram_1 (.in_1(in_1), .in_2(demultiplexer_1_out0), .in_3(in_3[1:0]), .out_4(n4ram_1_out_4));
  _4RAM u_4ram_2 (.in_1(in_1), .in_2(demultiplexer_1_out1), .in_3(in_3[1:0]), .out_4(n4ram_2_out_4));
  _4RAM u_4ram_3 (.in_1(in_1), .in_2(demultiplexer_1_out2), .in_3(in_3[1:0]), .out_4(n4ram_3_out_4));
  _4RAM u_4ram_4 (.in_1(in_1), .in_2(demultiplexer_1_out3), .in_3(in_3[1:0]), .out_4(n4ram_4_out_4));
  Multiplexer #(.select(2), .width(16), .enable("false")) multiplexer_1 (
    .in0(n4ram_1_out_4), .in1(n4ram_2_out_4), .in2(n4ram_3_out_4), .in3(n4ram_4_out_4), .out(out_4),
    .sel(in_3[3:2]));
endmodule

module CPU (
  input  [15:0] in_1,
  input  [15:0] in_2,
  input  in_3,
  output out_4,
  output [15:0] out_5,
  output [15:0] out_6,
  output [15:0] out_7
);

  wire alu_1_out_9, alu_1_out_11, and_1_out, and_2_out, and_3_out, and_4_out, nand_1_out, nor_1_out,
       not_1_out, not_2_out, not_3_out, or_1_out;
  wire [15:0] multiplexer_1_out, multiplexer_2_out, register_2_out_3;

  not not_1 (not_1_out, in_1[5]);
  nand nand_1 (nand_1_out, not_1_out, in_1[15]);
  Multiplexer #(.width(16), .enable("false")) multiplexer_1 (
    .in0(in_1), .in1(out_5), .out(multiplexer_1_out), .sel(in_1[15]));
  Register register_1 (.in_1(nand_1_out), .in_2(multiplexer_1_out), .out_3(out_6));
  Register register_2 (.in_1(in_1[4]), .in_2(out_5), .out_3(register_2_out_3));
  or or_1 (or_1_out, and_2_out, and_3_out, and_4_out);
  and and_1 (and_1_out, in_1[15], or_1_out);
  nor nor_1 (nor_1_out, in_3, and_1_out);
  Multiplexer #(.width(16), .enable("false")) multiplexer_2 (
    .in0(out_6), .in1(in_2), .out(multiplexer_2_out), .sel(in_1[12]));
  and and_2 (and_2_out, in_1[2], alu_1_out_11, alu_1_out_9);
  PC pc_1 (.in_1(nor_1_out), .in_2(and_1_out), .in_3(in_3), .in_4(out_6), .out_5(out_7));
  and and_3 (and_3_out, in_1[1], alu_1_out_11, not_3_out);
  not not_2 (not_2_out, alu_1_out_11);
  and and_4 (and_4_out, in_1[0], not_2_out, not_3_out);
  not not_3 (not_3_out, alu_1_out_9);
  ALU alu_1 (
    .in_1(register_2_out_3), .in_2(in_1[11]), .in_3(in_1[10]), .in_4(multiplexer_2_out), .in_5(in_1[9]),
    .in_6(in_1[8]), .in_7(in_1[7]), .in_8(in_1[6]), .out_9(alu_1_out_9), .out_10(out_5), .out_11(alu_1_out_11));

  assign out_4 = in_1[3];

  // Notes on the sheet:
  //   writeM
endmodule

module PC (
  input  in_1,
  input  in_2,
  input  in_3,
  input  [15:0] in_4,
  output [15:0] out_5
);

  wire [15:0] multiplexer_1_out, multiplexer_2_out, multiplexer_3_out, n16adder_1_out_3;

  Multiplexer #(.width(16), .enable("false")) multiplexer_1 (
    .in0(out_5), .in1(n16adder_1_out_3), .out(multiplexer_1_out), .sel(in_1));
  Multiplexer #(.width(16), .enable("false")) multiplexer_2 (
    .in0(multiplexer_1_out), .in1(in_4), .out(multiplexer_2_out), .sel(in_2));
  Multiplexer #(.width(16), .enable("false")) multiplexer_3 (
    .in0(multiplexer_2_out), .in1({16{1'b0}}), .out(multiplexer_3_out), .sel(in_3));
  _16adder u_16adder_1 (.in_1(out_5), .in_2(16'h1), .out_3(n16adder_1_out_3));
  Register register_1 (.in_1(1'b1), .in_2(multiplexer_3_out), .out_3(out_5));
endmodule

module hack (
  input  in_1,
  input  [31:0] in_2
);

  wire clock_1_out, cpu_1_out_4;
  wire [15:0] cpu_1_out_5, cpu_1_out_6, cpu_1_out_7, ram_1_data, ram_2_data;

  Clock clock_1 (.out(clock_1_out));
  RAM #(.addrWidth(16), .dataWidth(16)) ram_1 (
    .addr(cpu_1_out_7), .data(ram_1_data), .clk(clock_1_out), .ld(1'b1));  // open: sel, clr
  DotMatrix #(.matrixcols(32), .matrixrows(32)) dotmatrix_1 (.col0(in_2));  // open: col1, col2, col3, col4, col5, col6, col7, col8, col9, col10, col11, col12, col13, col14, col15, col16, col17, col18, col19, col20, col21, col22, col23, col24, col25, col26, col27, col28, col29, col30, col31
  CPU cpu_1 (
    .in_1(ram_1_data), .in_3(in_1), .out_4(cpu_1_out_4), .out_5(cpu_1_out_5), .out_6(cpu_1_out_6),
    .out_7(cpu_1_out_7), .in_2(ram_2_data));
  RAM #(.addrWidth(16), .dataWidth(16), .bus("separate")) ram_2 (
    .addr(cpu_1_out_6), .din(cpu_1_out_5), .data(ram_2_data), .str(cpu_1_out_4), .clk(clock_1_out), .ld(1'b1));  // open: sel, clr
endmodule
